# Fritzing sketch Measurements_Proj (saved by Fritzing 0.9.9b)
breadboards: 1

parts:
  U1 = Turbidity Sensor Probe [package=THT]
  A1 = TS-300B interface
  U2 = NodeMCU V1.0
  LED1 = LED - 3mm [color="Green (560nm)" package="3 mm [THT]"]
  R1 = Resistor [tolerance=±5% resistance=2200 package="2010 [SMD]"]

nets:
  N1: U1.pin1, A1.Pin_5
  N2: U1.pin2, A1.Pin_6
  N3: U1.VCC, A1.Pin_7
  N4: A1.Pin_1, A1.Pin_8, U2.GND, R1.Pin_0
  N5: A1.Pin_2, U2.A0
  N6: A1.Pin_4, U2.Vin
  N7: U2.D2, LED1.anode
  N8: LED1.cathode, R1.Pin_1

custom parts:
  Turbidity Sensor Probe: Turbidity sensor probe to the DFRobot measure module.
  TS-300B interface: TS-300B interface.
  NodeMCU V1.0: ESP8266 based NodeMCU
